# Fritzing sketch step4 (saved by Fritzing 0.9.2b)
breadboards: 1

parts:
  Part1 = Arduino Leonardo (Rev3b)
  LED1 = LED - 5mm [color="Red (633nm)" package="5 mm [THT]"]
  R1 = Resistor [tolerance=±5% resistance=220 package="0402 [SMD]"]
  R5 = Resistor [tolerance=±5% resistance=10k package=THT]
  R6 = Photocell (LDR) [package=THT]

nets:
  N1: Part1.5V, R6.pin_0
  N2: Part1.GND, LED1.cathode, R5.Pin_0
  N3: Part1.A2, R5.Pin_1, R6.pin_1
  N4: Part1.D13_PWM, R1.Pin_1
  N5: LED1.anode, R1.Pin_0
